// Logisim project cpu.circ as structural Verilog: 1 circuit, main circuit cpu
module cpu (
  input  clk,
  input  [31:0] INSTRUCTION,
  input  [31:0] READ_DATA,
  output [31:0] WRITE_ADDRESS,
  output [31:0] PROGRAM_COUNTER,
  output [31:0] ra,
  output [31:0] sp,
  output [31:0] t0,
  output [31:0] t1,
  output [31:0] t2,
  output [31:0] s0,
  output [31:0] s1,
  output [31:0] a0,
  output [31:0] tohost,
  output [3:0] WRITE_ENABLE,
  output [31:0] WRITE_DATA
);

  wire [2:0] funct3;
  wire [31:0] adder_1_out, adder_2_out, imm, inst, PC, ReadData1, Result, undriven, WriteData;

  Adder #(.width(32)) adder_1 (.a(PROGRAM_COUNTER), .b(32'h4), .out(adder_1_out));  // open: cin, cout
  Register #(.width(32)) u_PC (.D(adder_1_out), .clk(clk), .Q(PROGRAM_COUNTER));  // open: en, clr
  // control_logic control_logic_1: pin names not known
  Register #(.width(32)) PC_ID (.D(PROGRAM_COUNTER), .en(1'b1), .clk(clk), .Q(PC));  // open: clr
  Register #(.width(32)) inst_ID (
    .D(INSTRUCTION), .en(1'b1), .clk(clk), .Q({inst[31:15], funct3, inst[11:0]}));  // open: clr
  // branch_comp branch_comp_1: pin names not known
  imm_gen imm_gen_1 (.inst({inst[31:15], funct3, inst[11:0]}), .imm(imm));  // open: ImmSel
  csr csr_1 (.tohost(tohost));  // open: CSR_address, CSR_din, CSR_WE, clk
  regfile regfile_1 (
    .rs1(inst[19:15]), .rd(inst[11:7]), .Write_Data(WriteData), .RegWEn(1'b1), .clk(clk), .ra(ra), .sp(sp),
    .t0(t0), .t1(t1), .t2(t2), .s0(s0), .s1(s1), .a0(a0), .Read_Data_1(ReadData1));  // open: rs2, Read_Data_2
  alu alu_1 (.Result(Result), .A(ReadData1), .B(imm), .ALUSel(4'b0000));
  Adder #(.width(32)) adder_2 (.a(undriven), .b(32'h4), .out(adder_2_out));  // open: cin, cout
  Multiplexer #(.enable("false"), .select(2), .width(32)) multiplexer_1 (
    .in0(Result), .in1(READ_DATA), .in2(adder_2_out), .out(WriteData), .sel(2'b00));  // open: in3

  // Other names for the same wires on the sheet: opcode[6:0] = inst[6:0]; rd[4:0] = inst[11:7]; inst[14:12] = funct3;
  //   rs1[4:0] = inst[19:15]

  // Notes on the sheet:
  //   Output to IMEM
  //   IMEM (do **NOT** move this)
  //   Inputs from IMEM
  //   It is OK to move the PC, RegFile, ALU, MEM, Branch Comp, Imm Gen, and Control Logic to wherever is most convenient for you when constructing your CPU, and to delete this text
  //   Inputs/Outputs for testing. Do **NOT** move these.
  //   Outputs To DMEM
  //   DMEM (do **NOT** move this)
  //   Inputs From DMEM
endmodule
